// Logisim project xor.circ as structural Verilog: 1 circuit, main circuit main
module main (
  input  in_1,
  input  in_2,
  output out_3
);

  wire transistor_1_out, transistor_3_out, transistor_5_out, transistor_7_out, transistor_8_out,
       transistor_10_out, transistor_12_out, transistor_15_out, transistor_17_out, transistor_18_out;

  Transistor transistor_1 (.in(1'b1), .out(transistor_1_out), .gate(in_1));
  Transistor #(.\type ("n")) transistor_2 (.in(1'b0), .out(transistor_1_out), .gate(in_1));
  Transistor transistor_3 (.in(1'b1), .out(transistor_3_out), .gate(in_2));
  Transistor #(.\type ("n")) transistor_4 (.in(1'b0), .out(transistor_3_out), .gate(in_2));
  Transistor transistor_5 (.in(1'b1), .out(transistor_5_out), .gate(transistor_1_out));
  Transistor #(.\type ("n")) transistor_6 (.in(transistor_7_out), .out(transistor_5_out), .gate(transistor_1_out));
  Transistor #(.\type ("n")) transistor_7 (.in(1'b0), .out(transistor_7_out), .gate(in_2));
  Transistor transistor_8 (.in(1'b1), .out(transistor_8_out), .gate(transistor_3_out));
  Transistor #(.\type ("n")) transistor_9 (.in(transistor_10_out), .out(transistor_8_out), .gate(transistor_3_out));
  Transistor #(.\type ("n")) transistor_10 (.in(1'b0), .out(transistor_10_out), .gate(in_1));
  Transistor transistor_11 (.in(1'b1), .out(transistor_5_out), .gate(in_2));
  Transistor transistor_12 (.in(1'b1), .out(transistor_12_out), .gate(transistor_5_out));
  Transistor #(.\type ("n")) transistor_13 (.in(1'b0), .out(transistor_12_out), .gate(transistor_5_out));
  Transistor transistor_14 (.in(1'b1), .out(transistor_8_out), .gate(in_1));
  Transistor transistor_15 (.in(1'b1), .out(transistor_15_out), .gate(transistor_8_out));
  Transistor #(.\type ("n")) transistor_16 (.in(1'b0), .out(transistor_15_out), .gate(transistor_8_out));
  Transistor #(.\type ("n")) transistor_17 (.in(1'b0), .out(transistor_17_out), .gate(transistor_15_out));
  Transistor transistor_18 (.in(1'b1), .out(transistor_18_out), .gate(transistor_12_out));
  Transistor transistor_19 (.in(transistor_18_out), .out(transistor_17_out), .gate(transistor_15_out));
  Transistor #(.\type ("n")) transistor_20 (.in(1'b0), .out(transistor_17_out), .gate(transistor_12_out));
  Transistor transistor_21 (.in(1'b1), .out(out_3), .gate(transistor_17_out));
  Transistor #(.\type ("n")) transistor_22 (.in(1'b0), .out(out_3), .gate(transistor_17_out));

  // Other names for the same wires on the sheet: A = in_1; B = in_2

  // Notes on the sheet:
  //   Not Gate
  //   Not Gate
  //   And Gate
  //   And Gate
  //   Xor Gate - ~A&B or A&~B
  //   ~A&B
  //   A&~b
  //   Or Gate
endmodule
